// Logisim project D FlipFlop.circ as structural Verilog: 2 circuits, main circuit main
module main (
  input  in_1,
  input  in_2,
  output out_3,
  output out_4
);

  wire nand_1_out, nand_2_out, not_1_out;

  not not_1 (not_1_out, in_2);
  nand nand_1 (nand_1_out, in_1, not_1_out);
  nand nand_2 (nand_2_out, nand_1_out, not_1_out);
  nand nand_3 (out_3, nand_1_out, out_4);
  nand nand_4 (out_4, out_3, nand_2_out);
endmodule

module D_flipflop (
  input  in_1,
  input  in_2,
  output out_3,
  output out_4
);

  wire main_1_p3, main_2_p3, main_3_p3;

  // main main_1: pin names not known; wires that end beside it: in_1, in_2, main_1_p3
  // main main_2: pin names not known; wires that end beside it: main_1_p3, in_2, main_2_p3
  // main main_3: pin names not known; wires that end beside it: main_2_p3, in_2, main_3_p3
  // main main_4: pin names not known; wires that end beside it: main_3_p3, in_2, out_3, out_4
endmodule
