// Logisim project comparator.circ as structural Verilog: 2 circuits, main circuit main
module main (
  input  A,
  input  in_2,
  output out_3,
  output out_4,
  output out_5
);

  wire not_1_out, not_2_out;

  not not_1 (not_1_out, in_2);
  not not_2 (not_2_out, A);
  and Gate_1 (out_3, A, not_1_out);
  xnor Gate_2 (out_4, A, in_2);
  and Gate_3 (out_5, in_2, not_2_out);

  // Notes on the sheet:
  //   b
endmodule

module Ic (
  input  in_1,
  input  in_2,
  output out_3,
  output out_4,
  output out_5
);

  main main_1 (.A(in_1), .in_2(in_2), .out_3(out_3), .out_4(out_4), .out_5(out_5));
endmodule
