// Logisim project mux.circ as structural Verilog: 2 circuits, main circuit main
module main (
  input  in_1,
  input  in_2,
  input  in_3,
  output out_4
);

  wire nand_1_out, nand_2_out, nand_3_out;

  nand nand_1 (nand_1_out, in_2, in_2);
  nand nand_2 (nand_2_out, in_1, in_2);
  nand nand_3 (nand_3_out, nand_1_out, in_3);
  nand nand_4 (out_4, nand_2_out, nand_3_out);
endmodule

module _4x1 (
  input  in_1,
  input  in_2,
  input  in_3,
  input  in_4,
  input  in_5,
  output out_6
);

  wire main_1_out_4, Mux_out_4;

  main Mux (.in_1(in_1), .in_2(in_2), .in_3(in_5), .out_4(Mux_out_4));
  main main_1 (.in_1(in_3), .in_2(in_4), .in_3(in_5), .out_4(main_1_out_4));
  main main_2 (.in_1(Mux_out_4), .in_2(main_1_out_4), .in_3(in_5), .out_4(out_6));
endmodule
